# Fritzing sketch Display4digAlhambra (saved by Fritzing 0.8.7b)
breadboards: 1

parts:
  U1 = 7-SEGMENT-4DIGIT [package=7-segment-4digit-youngsun]
  R3 = Resistor [tolerance=±5% resistance=220 package=THT]
  R4 = Resistor [tolerance=±5% resistance=220 package=THT]
  R5 = Resistor [tolerance=±5% resistance=220 package=THT]
  R6 = Resistor [tolerance=±5% resistance=220 package=THT]
  Parte1 = iceZUM Alhambra

nets:
  N1: U1.3, Parte1.D4
  N2: U1.4, Parte1.D3
  N3: U1.6, Parte1.D2
  N4: U1.7, Parte1.D6
  N5: U1.8, R6.Pin_0
  N6: U1.9, Parte1.D1
  N7: U1.11, R4.Pin_1
  N8: U1.13, Parte1.D0
  N9: U1.14, R5.Pin_1
  N10: R3.Pin_0, Parte1.D11
  N11: R4.Pin_0, Parte1.D12
  N12: R5.Pin_0, Parte1.D13
  N13: R6.Pin_1, Parte1.D10
  N14: Parte1.DD0, Parte1.DD1
  N15: Parte1.VD0, Parte1.VD1

notes:
  Erresistentziak 1000 Ohm-ekoak dira.

custom parts:
  iceZUM Alhambra: Arduino/zum compatible Open FPGA electronic board. Synthesize hardware easily, using only open source tools
